// Logisim project CRC.circ as structural Verilog: 2 circuits, main circuit CRC
module CRC (
  input  [7:0] A,
  input  [3:0] B,
  output [10:0] C
);

  wire [2:0] n4bit_mod2_3_c, n4bit_mod2_4_c, n4bit_mod2_5_c, n4bit_mod2_7_c, n4bit_mod2_8_c;
  wire [3:1] n4bit_mod2_1_c, n4bit_mod2_2_c;

  _4bit_mod2 u_4bit_mod2_1 (.A(A[7:4]), .B(B), .C(n4bit_mod2_1_c));  // open: out_3
  _4bit_mod2 u_4bit_mod2_2 (.A({n4bit_mod2_8_c, 1'b0}), .B(B), .C(n4bit_mod2_2_c));  // open: out_3
  _4bit_mod2 u_4bit_mod2_3 (.A({n4bit_mod2_1_c, A[3]}), .B(B), .C(n4bit_mod2_3_c));  // open: out_3
  _4bit_mod2 u_4bit_mod2_4 (.A({n4bit_mod2_2_c, 1'b0}), .B(B), .C(n4bit_mod2_4_c));  // open: out_3
  _4bit_mod2 u_4bit_mod2_5 (.A({n4bit_mod2_3_c, A[2]}), .B(B), .C(n4bit_mod2_5_c));  // open: out_3
  _4bit_mod2 u_4bit_mod2_6 (.A({n4bit_mod2_4_c, 1'b0}), .B(B), .C(C[2:0]));  // open: out_3
  // Probe on C[2:0]
  _4bit_mod2 u_4bit_mod2_7 (.A({n4bit_mod2_5_c, A[1]}), .B(B), .C(n4bit_mod2_7_c));  // open: out_3
  _4bit_mod2 u_4bit_mod2_8 (.A({n4bit_mod2_7_c, A[0]}), .B(B), .C(n4bit_mod2_8_c));  // open: out_3

  assign C[10:3] = A;

  // Other names for the same wires on the sheet: _4 = A[1]; _5 = A[0]; remainder[2:0] = C[2:0]; _3 = A[2]; _2 = A[3];
  //   _1[3:0] = A[7:4]
endmodule

// mod
module _4bit_mod2 (
  input  [3:0] A,
  input  [3:0] B,
  output out_3,
  output [2:0] C
);

  wire [3:0] xor_1_out;
  wire [3:3] multiplexer_1_out;

  assign xor_1_out = A ^ B;  // XOR_Gate xor_1, 4 bits wide
  Multiplexer #(.width(4)) multiplexer_1 (
    .in0(A), .in1(xor_1_out), .out({multiplexer_1_out[3], C}), .sel(A[3]));  // open: en

  assign out_3 = A[3];
endmodule
