// Logisim project FSM.circ as structural Verilog: 3 circuits, main circuit fsm
module fsm (
  input  CLR,
  input  [1:0] In,
  output Z
);

  wire clock_1_out;
  wire [1:0] multiplexer_1_out, register_1_q, transfer_1_b;

  transfer transfer_1 (.a(register_1_q), .In(In), .b(transfer_1_b));
  Multiplexer #(.width(2)) multiplexer_1 (
    .in0(transfer_1_b), .in1(2'b00), .out(multiplexer_1_out), .sel(CLR));  // open: en
  Register #(.width(2)) register_1 (.D(multiplexer_1_out), .Q(register_1_q), .clk(clock_1_out));  // open: en, clr
  Clock clock_1 (.out(clock_1_out));
  \output  output_1 (.a(register_1_q), .In(In), .out(Z));
endmodule

// out
module \output  (
  input  [1:0] a,
  input  [1:0] In,
  output out
);

  wire not_1_out, not_2_out;

  not not_1 (not_1_out, a[0]);
  not not_2 (not_2_out, In[0]);
  and and_1 (out, a[1], not_1_out, not_2_out);
endmodule

// tran
module transfer (
  input  [1:0] a,
  input  [1:0] In,
  output [1:0] b
);

  wire and_1_out, and_2_out, and_3_out, and_4_out, not_1_out, not_2_out, not_3_out, not_4_out, not_5_out,
       not_6_out, not_7_out;

  not not_1 (not_1_out, a[1]);
  not not_2 (not_2_out, In[0]);
  not not_3 (not_3_out, a[0]);
  not not_4 (not_4_out, In[0]);
  not not_5 (not_5_out, In[1]);
  not not_6 (not_6_out, a[0]);
  not not_7 (not_7_out, In[0]);
  and and_1 (and_1_out, not_1_out, a[0], not_2_out);
  and and_2 (and_2_out, a[1], not_3_out, not_4_out);
  and and_3 (and_3_out, not_5_out, In[0]);
  and and_4 (and_4_out, a[1], not_6_out, not_7_out);
  or or_1 (b[1], and_1_out, and_2_out);
  or or_2 (b[0], and_3_out, and_4_out);
endmodule
