// Logisim project GRF.circ as structural Verilog: 1 circuit, main circuit grf
module grf (
  input  in_1,
  input  in_2,
  input  [31:0] WD,
  input  WE,
  input  [4:0] A3,
  input  [4:0] A1,
  input  [4:0] A2,
  output [31:0] RD1,
  output [31:0] RD2
);

  wire [31:0] d1, d2, d3, d4, d5, d6, d7, d8, d9, d10, d11, d12, d13, d14, d15, d16, d17, d18, d19, d20, d21,
       d22, d23, d24, d25, d26, d27, d28, d29, d30, d31, d32, q1, q2, q3, q4, q5, q6, q7, q8, q9, q10, q11,
       q12, q13, q14, q15, q16, q17, q18, q19, q20, q21, q22, q23, q24, q25, q26, q27, q28, q29, q30, q31,
       q32;

  Demultiplexer #(.select(5), .width(32), .tristate("true")) demultiplexer_1 (
    .out0(d1), .out1(d2), .out2(d3), .out3(d4), .out4(d5), .out5(d6), .out6(d7), .out7(d8), .out8(d9),
    .out9(d10), .out10(d11), .out11(d12), .out12(d13), .out13(d14), .out14(d15), .out15(d16), .out16(d17),
    .out17(d18), .out18(d19), .out19(d20), .out20(d21), .out21(d22), .out22(d23), .out23(d24), .out24(d25),
    .out25(d26), .out26(d27), .out27(d28), .out28(d29), .out29(d30), .out30(d31), .out31(d32), .in(WD),
    .sel(A3), .en(WE));
  Register #(.width(32)) register_1 (.D({32{1'b0}}), .Q(q1), .clk(in_1), .clr(in_2));  // open: en
  Register #(.width(32)) register_2 (.D(d14), .Q(q14), .clk(in_1), .clr(in_2));  // open: en
  Register #(.width(32)) register_3 (.D(d26), .Q(q26), .clk(in_1), .clr(in_2));  // open: en
  Register #(.width(32)) register_4 (.D(d2), .Q(q2), .clk(in_1), .clr(in_2));  // open: en
  Register #(.width(32)) register_5 (.D(d15), .Q(q15), .clk(in_1), .clr(in_2));  // open: en
  Register #(.width(32)) register_6 (.D(d27), .Q(q27), .clk(in_1), .clr(in_2));  // open: en
  Register #(.width(32)) register_7 (.D(d16), .Q(q16), .clk(in_1), .clr(in_2));  // open: en
  Register #(.width(32)) register_8 (.D(d28), .Q(q28), .clk(in_1), .clr(in_2));  // open: en
  Register #(.width(32)) register_9 (.D(d3), .Q(q3), .clk(in_1), .clr(in_2));  // open: en
  Register #(.width(32)) register_10 (.D(d4), .Q(q4), .clk(in_1), .clr(in_2));  // open: en
  Register #(.width(32)) register_11 (.D(d17), .Q(q17), .clk(in_1), .clr(in_2));  // open: en
  Register #(.width(32)) register_12 (.D(d29), .Q(q29), .clk(in_1), .clr(in_2));  // open: en
  Register #(.width(32)) register_13 (.D(d5), .Q(q5), .clk(in_1), .clr(in_2));  // open: en
  Register #(.width(32)) register_14 (.D(d18), .Q(q18), .clk(in_1), .clr(in_2));  // open: en
  Register #(.width(32)) register_15 (.D(d30), .Q(q30), .clk(in_1), .clr(in_2));  // open: en
  Multiplexer #(.select(5), .width(32), .enable("false")) multiplexer_1 (
    .in0(q1), .in1(q2), .in2(q3), .in3(q4), .in4(q5), .in5(q6), .in6(q7), .in7(q8), .in8(q9), .in9(q10),
    .in10(q11), .in11(q12), .in12(q13), .in13(q14), .in14(q15), .in15(q16), .in16(q17), .in17(q18),
    .in18(q19), .in19(q20), .in20(q21), .in21(q22), .in22(q23), .in23(q24), .in24(q25), .in25(q26),
    .in26(q27), .in27(q28), .in28(q29), .in29(q30), .in30(q31), .in31(q32), .out(RD1), .sel(A1));
  Register #(.width(32)) register_16 (.D(d6), .Q(q6), .clk(in_1), .clr(in_2));  // open: en
  Register #(.width(32)) register_17 (.D(d19), .Q(q19), .clk(in_1), .clr(in_2));  // open: en
  Register #(.width(32)) register_18 (.D(d31), .Q(q31), .clk(in_1), .clr(in_2));  // open: en
  Register #(.width(32)) register_19 (.D(d7), .Q(q7), .clk(in_1), .clr(in_2));  // open: en
  Register #(.width(32)) register_20 (.D(d20), .Q(q20), .clk(in_1), .clr(in_2));  // open: en
  Register #(.width(32)) register_21 (.D(d32), .Q(q32), .clk(in_1), .clr(in_2));  // open: en
  Register #(.width(32)) register_22 (.D(d8), .Q(q8), .clk(in_1), .clr(in_2));  // open: en
  Register #(.width(32)) register_23 (.D(d21), .Q(q21), .clk(in_1), .clr(in_2));  // open: en
  Register #(.width(32)) register_24 (.D(d9), .Q(q9), .clk(in_1), .clr(in_2));  // open: en
  Register #(.width(32)) register_25 (.D(d22), .Q(q22), .clk(in_1), .clr(in_2));  // open: en
  Multiplexer #(.select(5), .width(32), .enable("false")) multiplexer_2 (
    .in0(q1), .in1(q2), .in2(q3), .in3(q4), .in4(q5), .in5(q6), .in6(q7), .in7(q8), .in8(q9), .in9(q10),
    .in10(q11), .in11(q12), .in12(q13), .in13(q14), .in14(q15), .in15(q16), .in16(q17), .in17(q18),
    .in18(q19), .in19(q20), .in20(q21), .in21(q22), .in22(q23), .in23(q24), .in24(q25), .in25(q26),
    .in26(q27), .in27(q28), .in28(q29), .in29(q30), .in30(q31), .in31(q32), .out(RD2), .sel(A2));
  Register #(.width(32)) register_26 (.D(d10), .Q(q10), .clk(in_1), .clr(in_2));  // open: en
  Register #(.width(32)) register_27 (.D(d23), .Q(q23), .clk(in_1), .clr(in_2));  // open: en
  Register #(.width(32)) register_28 (.D(d11), .Q(q11), .clk(in_1), .clr(in_2));  // open: en
  Register #(.width(32)) register_29 (.D(d24), .Q(q24), .clk(in_1), .clr(in_2));  // open: en
  Register #(.width(32)) register_30 (.D(d12), .Q(q12), .clk(in_1), .clr(in_2));  // open: en
  Register #(.width(32)) register_31 (.D(d25), .Q(q25), .clk(in_1), .clr(in_2));  // open: en
  Register #(.width(32)) register_32 (.D(d13), .Q(q13), .clk(in_1), .clr(in_2));  // open: en

  // Other names for the same wires on the sheet: clk = in_1; reset = in_2
endmodule
