// Logisim project navigation.circ as structural Verilog: 3 circuits, main circuit navigation
module navigation (
  input  [1:0] dir,
  input  clk,
  input  reset,
  output arrive,
  output hit
);

  wire [2:0] register_1_q;
  wire [3:0] tran_1_b0;

  \tran  tran_1 (
    .a2(register_1_q[2]), .a1(register_1_q[1]), .a0(register_1_q[0]), .i1(dir[1]), .i0(dir[0]),
    .b2(tran_1_b0[2]), .b1(tran_1_b0[1]), .b0(tran_1_b0[0]), .hit(tran_1_b0[3]));
  Register #(.width(4)) register_1 (.D(tran_1_b0), .Q({hit, register_1_q}), .clk(clk), .clr(reset));  // open: en
  out out_1 (.a2(register_1_q[2]), .a1(register_1_q[1]), .a0(register_1_q[0]), .arrive(arrive));
endmodule

module \tran  (
  input  a2,
  input  a1,
  input  a0,
  input  i1,
  input  i0,
  output b2,
  output b1,
  output b0,
  output hit
);

  wire and_1_out, and_2_out, and_3_out, and_4_out, and_5_out, and_6_out, and_7_out, and_8_out, and_9_out,
       and_10_out, and_11_out, and_12_out, and_13_out, and_14_out, and_15_out, and_16_out, not_1_out,
       not_2_out, not_3_out, not_4_out, not_5_out, not_6_out, not_7_out, not_8_out, not_9_out, not_10_out,
       not_11_out, not_12_out, not_13_out, not_14_out, not_15_out, not_16_out, not_17_out, not_18_out,
       not_19_out, not_20_out, not_21_out, not_22_out, not_23_out, not_24_out, not_25_out, not_26_out,
       not_27_out, not_28_out, not_29_out, not_30_out, not_31_out, not_32_out, not_33_out, not_34_out,
       not_35_out, not_36_out, not_37_out, not_38_out, not_39_out, not_40_out;

  not not_1 (not_1_out, a2);
  not not_2 (not_2_out, a0);
  not not_3 (not_3_out, i1);
  not not_4 (not_4_out, a2);
  not not_5 (not_5_out, i1);
  not not_6 (not_6_out, i0);
  not not_7 (not_7_out, a2);
  not not_8 (not_8_out, i1);
  not not_9 (not_9_out, a2);
  not not_10 (not_10_out, i1);
  not not_11 (not_11_out, a2);
  not not_12 (not_12_out, a0);
  not not_13 (not_13_out, a2);
  not not_14 (not_14_out, i0);
  not not_15 (not_15_out, a2);
  not not_16 (not_16_out, a1);
  not not_17 (not_17_out, a0);
  not not_18 (not_18_out, i1);
  not not_19 (not_19_out, i0);
  not not_20 (not_20_out, a2);
  not not_21 (not_21_out, a2);
  not not_22 (not_22_out, i0);
  not not_23 (not_23_out, a2);
  not not_24 (not_24_out, a1);
  not not_25 (not_25_out, a0);
  not not_26 (not_26_out, a2);
  not not_27 (not_27_out, a1);
  not not_28 (not_28_out, a0);
  not not_29 (not_29_out, a2);
  not not_30 (not_30_out, a1);
  not not_31 (not_31_out, a2);
  not not_32 (not_32_out, a0);
  not not_33 (not_33_out, a2);
  not not_34 (not_34_out, a0);
  not not_35 (not_35_out, i1);
  not not_36 (not_36_out, i0);
  not not_37 (not_37_out, a2);
  not not_38 (not_38_out, i1);
  not not_39 (not_39_out, a2);
  not not_40 (not_40_out, i0);
  and and_1 (and_1_out, not_1_out, a1, not_2_out, not_3_out, i0);
  and and_2 (and_2_out, not_4_out, a1, a0, not_5_out, not_6_out);
  and and_3 (and_3_out, not_7_out, a0, not_8_out);
  and and_4 (and_4_out, not_9_out, a1, not_10_out);
  and and_5 (and_5_out, not_11_out, a1, not_12_out, i0);
  and and_6 (and_6_out, not_13_out, a1, a0, not_14_out);
  and and_7 (and_7_out, not_15_out, not_16_out, not_17_out, not_18_out, not_19_out);
  and and_8 (and_8_out, not_20_out, a0, i0);
  and and_9 (and_9_out, not_21_out, a1, i1, not_22_out);
  and and_10 (and_10_out, not_23_out, not_24_out, not_25_out, i0);
  and and_11 (and_11_out, not_26_out, not_27_out, not_28_out, i1);
  and and_12 (and_12_out, not_29_out, not_30_out, i1, i0);
  and and_13 (and_13_out, not_31_out, not_32_out, i1, i0);
  and and_14 (and_14_out, not_33_out, a1, not_34_out, not_35_out, not_36_out);
  and and_15 (and_15_out, not_37_out, a1, a0, not_38_out, i0);
  and and_16 (and_16_out, not_39_out, a1, a0, i1, not_40_out);
  or or_1 (b2, and_1_out, and_2_out);
  or or_2 (b1, and_3_out, and_4_out, and_5_out, and_6_out);
  or or_3 (b0, and_7_out, and_8_out, and_9_out);
  or or_4 (hit, and_10_out, and_11_out, and_12_out, and_13_out, and_14_out, and_15_out, and_16_out);
endmodule

module out (
  input  a2,
  input  a1,
  input  a0,
  output arrive
);

  wire not_1_out;

  not not_1 (not_1_out, a0);
  and and_1 (arrive, a2, a1, not_1_out);
endmodule
