// Logisim project singleCycle.circ as structural Verilog: 6 circuits, main circuit ALU
module ALU (
  input  [31:0] SrcA,
  input  [31:0] SrcB,
  input  [1:0] ALUOp,
  output Zero,
  output [31:0] ALUResult
);

  wire [31:0] adder_1_out, and_1_out, or_1_out, subtractor_1_out;

  Adder #(.width(32)) adder_1 (.a(SrcA), .b(SrcB), .out(adder_1_out));  // open: cin, cout
  Subtractor #(.width(32)) subtractor_1 (.a(SrcA), .b(SrcB), .out(subtractor_1_out));  // open: bin, bout
  assign or_1_out = SrcA | SrcB;  // OR_Gate or_1, 32 bits wide
  assign and_1_out = SrcA & SrcB;  // AND_Gate and_1, 32 bits wide
  Multiplexer #(.select(2), .width(32)) multiplexer_1 (
    .in0(adder_1_out), .in1(subtractor_1_out), .in2(or_1_out), .in3(and_1_out), .out(ALUResult), .sel(ALUOp));  // open: en
  Comparator #(.width(32)) comparator_1 (.a({32{1'b0}}), .b(ALUResult), .eq(Zero));  // open: gt, lt
endmodule

module main (
  input  Reset,
  output out_2,
  output out_3,
  output [31:0] out_4,
  output [4:0] out_5,
  output [4:0] out_6,
  output [31:0] out_7,
  output [31:0] out_8
);

  wire Clk, controller_1_alusrc, not_1_out, Zero;
  wire [1:0] controller_1_aluop, controller_1_extop, controller_1_regdst, controller_1_wdsrc, NPCOp;
  wire [31:0] alu_1_aluresult, ext_1_extimm, multiplexer_2_out, npc_1_npc, PC4, PC_q, ram_1_data, RD1;

  Clock clock_1 (.out(Clk));
  Register #(.width(32)) PC (.D(npc_1_npc), .Q(PC_q), .clk(Clk), .clr(Reset));  // open: en
  NPC npc_1 (.NPCOp(NPCOp), .PC(PC_q), .NPC(npc_1_npc), .PC4(PC4), .Imm(out_4[25:0]), .Zero(Zero), .RA(RD1));
  ROM #(.addrWidth(5), .dataWidth(32)) rom_1 (.addr(PC_q[6:2]), .data(out_4));  // open: sel
  Controller controller_1 (
    .Op(out_4[31:26]), .Func(out_4[5:0]), .RegWrite(out_2), .RegDst(controller_1_regdst),
    .ALUSrc(controller_1_alusrc), .NPCOp(NPCOp), .MemWrite(out_3), .WDSrc(controller_1_wdsrc),
    .EXTOp(controller_1_extop), .ALUOp(controller_1_aluop));
  Multiplexer #(.select(2), .width(5)) multiplexer_1 (
    .in0(out_4[20:16]), .in1(out_4[15:11]), .in2({5{1'b1}}), .out(out_5), .sel(controller_1_regdst));  // open: in3, en
  GRF grf_1 (
    .Clk(Clk), .Reset(Reset), .WD(out_7), .RD1(RD1), .WE(out_2), .A3(out_5), .A1(out_4[25:21]), .RD2(out_8),
    .A2(out_4[20:16]));
  EXT ext_1 (.Imm(out_4[15:0]), .EXTImm(ext_1_extimm), .EXTOp(controller_1_extop));
  ALU alu_1 (
    .SrcA(RD1), .SrcB(multiplexer_2_out), .Zero(Zero),
    .ALUResult({alu_1_aluresult[31:7], out_6, alu_1_aluresult[1:0]}), .ALUOp(controller_1_aluop));
  Multiplexer #(.width(32)) multiplexer_2 (
    .in0(out_8), .in1(ext_1_extimm), .out(multiplexer_2_out), .sel(controller_1_alusrc));  // open: en
  not not_1 (not_1_out, out_3);
  RAM #(.addrWidth(5), .dataWidth(32), .bus("separate")) ram_1 (
    .addr(out_6), .din(out_8), .data(ram_1_data), .str(out_3), .clk(Clk), .ld(not_1_out), .clr(Reset));  // open: sel
  Multiplexer #(.select(2), .width(32)) multiplexer_3 (
    .in0({alu_1_aluresult[31:7], out_6, alu_1_aluresult[1:0]}), .in1(ram_1_data), .in2(PC4), .out(out_7),
    .sel(controller_1_wdsrc));  // open: in3, en

  // Other names for the same wires on the sheet: MemAddr[4:0] = out_6; func[5:0] = out_4[5:0];
  //   imm16[15:0] = out_4[15:0]; imm26[25:0] = out_4[25:0]; Instr[31:0] = out_4; shamt[4:0] = out_4[10:6];
  //   rd[4:0] = out_4[15:11]; rt[4:0] = out_4[20:16]; rs[4:0] = out_4[25:21]; op[5:0] = out_4[31:26];
  //   MemData[31:0] = out_8; MemWrite = out_3; RegAddr[4:0] = out_5; RegData[31:0] = out_7; RegWrite = out_2

  // Notes on the sheet:
  //   contents of rom_1 (hex, n*v repeats v):
  //   3c06007b 3c07ffff 34e7ffff 34040001 c000c06 c43020 3e53022 3e00008
endmodule

module GRF (
  input  Clk,
  input  Reset,
  input  [31:0] WD,
  input  WE,
  input  [4:0] A3,
  input  [4:0] A1,
  input  [4:0] A2,
  output [31:0] RD1,
  output [31:0] RD2
);

  wire [31:0] d0, d1, d2, d3, d4, d5, d6, d7, d8, d9, d10, d11, d12, d13, d14, d15, d16, d17, d18, d19, d20,
       d21, d22, d23, d24, d25, d26, d27, d28, d29, d30, d31, o0, o1, o2, o3, o4, o5, o6, o7, o8, o9, o10,
       o11, o12, o13, o14, o15, o16, o17, o18, o19, o20, o21, o22, o23, o24, o25, o26, o27, o28, o29, o30,
       o31;

  Demultiplexer #(.select(5), .width(32), .tristate("true")) demultiplexer_1 (
    .out0(d0), .out1(d1), .out2(d2), .out3(d3), .out4(d4), .out5(d5), .out6(d6), .out7(d7), .out8(d8),
    .out9(d9), .out10(d10), .out11(d11), .out12(d12), .out13(d13), .out14(d14), .out15(d15), .out16(d16),
    .out17(d17), .out18(d18), .out19(d19), .out20(d20), .out21(d21), .out22(d22), .out23(d23), .out24(d24),
    .out25(d25), .out26(d26), .out27(d27), .out28(d28), .out29(d29), .out30(d30), .out31(d31), .in(WD),
    .sel(A3), .en(WE));
  Register #(.width(32)) register_1 (.D({32{1'b0}}), .Q(o0), .clk(Clk), .clr(Reset));  // open: en
  Register #(.width(32)) register_2 (.D(d14), .Q(o14), .clk(Clk), .clr(Reset));  // open: en
  Register #(.width(32)) register_3 (.D(d26), .Q(o26), .clk(Clk), .clr(Reset));  // open: en
  Register #(.width(32)) register_4 (.D(d2), .Q(o2), .clk(Clk), .clr(Reset));  // open: en
  Register #(.width(32)) register_5 (.D(d15), .Q(o15), .clk(Clk), .clr(Reset));  // open: en
  Register #(.width(32)) register_6 (.D(d27), .Q(o27), .clk(Clk), .clr(Reset));  // open: en
  Register #(.width(32)) register_7 (.D(d16), .Q(o16), .clk(Clk), .clr(Reset));  // open: en
  Register #(.width(32)) register_8 (.D(d28), .Q(o28), .clk(Clk), .clr(Reset));  // open: en
  Register #(.width(32)) register_9 (.D(d3), .Q(o3), .clk(Clk), .clr(Reset));  // open: en
  Register #(.width(32)) register_10 (.D(d4), .Q(o4), .clk(Clk), .clr(Reset));  // open: en
  Register #(.width(32)) register_11 (.D(d17), .Q(o17), .clk(Clk), .clr(Reset));  // open: en
  Register #(.width(32)) register_12 (.D(d29), .Q(o29), .clk(Clk), .clr(Reset));  // open: en
  Register #(.width(32)) register_13 (.D(d5), .Q(o5), .clk(Clk), .clr(Reset));  // open: en
  Register #(.width(32)) register_14 (.D(d18), .Q(o18), .clk(Clk), .clr(Reset));  // open: en
  Register #(.width(32)) register_15 (.D(d30), .Q(o30), .clk(Clk), .clr(Reset));  // open: en
  Multiplexer #(.select(5), .width(32), .enable("false")) multiplexer_1 (
    .in0(o0), .in1(o1), .in2(o2), .in3(o3), .in4(o4), .in5(o5), .in6(o6), .in7(o7), .in8(o8), .in9(o9),
    .in10(o10), .in11(o11), .in12(o12), .in13(o13), .in14(o14), .in15(o15), .in16(o16), .in17(o17),
    .in18(o18), .in19(o19), .in20(o20), .in21(o21), .in22(o22), .in23(o23), .in24(o24), .in25(o25),
    .in26(o26), .in27(o27), .in28(o28), .in29(o29), .in30(o30), .in31(o31), .out(RD1), .sel(A1));
  Register #(.width(32)) register_16 (.D(d6), .Q(o6), .clk(Clk), .clr(Reset));  // open: en
  Register #(.width(32)) register_17 (.D(d19), .Q(o19), .clk(Clk), .clr(Reset));  // open: en
  Register #(.width(32)) register_18 (.D(d31), .Q(o31), .clk(Clk), .clr(Reset));  // open: en
  Register #(.width(32)) register_19 (.D(d7), .Q(o7), .clk(Clk), .clr(Reset));  // open: en
  Register #(.width(32)) register_20 (.D(d20), .Q(o20), .clk(Clk), .clr(Reset));  // open: en
  Register #(.width(32)) register_21 (.D(d1), .Q(o1), .clk(Clk), .clr(Reset));  // open: en
  Register #(.width(32)) register_22 (.D(d8), .Q(o8), .clk(Clk), .clr(Reset));  // open: en
  Register #(.width(32)) register_23 (.D(d21), .Q(o21), .clk(Clk), .clr(Reset));  // open: en
  Register #(.width(32)) register_24 (.D(d9), .Q(o9), .clk(Clk), .clr(Reset));  // open: en
  Multiplexer #(.select(5), .width(32), .enable("false")) multiplexer_2 (
    .in0(o0), .in1(o1), .in2(o2), .in3(o3), .in4(o4), .in5(o5), .in6(o6), .in7(o7), .in8(o8), .in9(o9),
    .in10(o10), .in11(o11), .in12(o12), .in13(o13), .in14(o14), .in15(o15), .in16(o16), .in17(o17),
    .in18(o18), .in19(o19), .in20(o20), .in21(o21), .in22(o22), .in23(o23), .in24(o24), .in25(o25),
    .in26(o26), .in27(o27), .in28(o28), .in29(o29), .in30(o30), .in31(o31), .out(RD2), .sel(A2));
  Register #(.width(32)) register_25 (.D(d22), .Q(o22), .clk(Clk), .clr(Reset));  // open: en
  Register #(.width(32)) register_26 (.D(d10), .Q(o10), .clk(Clk), .clr(Reset));  // open: en
  Register #(.width(32)) register_27 (.D(d23), .Q(o23), .clk(Clk), .clr(Reset));  // open: en
  Register #(.width(32)) register_28 (.D(d11), .Q(o11), .clk(Clk), .clr(Reset));  // open: en
  Register #(.width(32)) register_29 (.D(d24), .Q(o24), .clk(Clk), .clr(Reset));  // open: en
  Register #(.width(32)) register_30 (.D(d12), .Q(o12), .clk(Clk), .clr(Reset));  // open: en
  Register #(.width(32)) register_31 (.D(d25), .Q(o25), .clk(Clk), .clr(Reset));  // open: en
  Register #(.width(32)) register_32 (.D(d13), .Q(o13), .clk(Clk), .clr(Reset));  // open: en
endmodule

module EXT (
  input  [15:0] Imm,
  input  [1:0] EXTOp,
  output [31:0] EXTImm
);

  wire [31:0] bit_extender_1_out, bit_extender_2_out;

  assign bit_extender_1_out = {{16{1'b0}}, Imm};  // Bit_Extender bit_extender_1
  assign bit_extender_2_out = {{16{Imm[15]}}, Imm};  // Bit_Extender bit_extender_2
  Multiplexer #(.select(2), .width(32)) multiplexer_1 (
    .in0(bit_extender_1_out), .in1(bit_extender_2_out), .in2({Imm, {16{1'b0}}}), .out(EXTImm), .sel(EXTOp));  // open: in3, en
endmodule

module Controller (
  input  [5:0] Op,
  input  [5:0] Func,
  output [1:0] NPCOp,
  output [1:0] EXTOp,
  output [1:0] RegDst,
  output [1:0] WDSrc,
  output RegWrite,
  output ALUSrc,
  output MemWrite,
  output [1:0] ALUOp
);

  wire A0, A1, and_1_out, and_2_out, and_3_out, and_4_out, and_5_out, beq_out, jal_out, jr_out, lui_out,
       lw_out, not_1_out, not_2_out, not_3_out, not_4_out, not_5_out, not_6_out, not_7_out, not_8_out,
       not_9_out, not_10_out, not_11_out, not_12_out, not_13_out, not_14_out, ori_out, R_out, sw_out;

  not not_1 (not_1_out, A0);
  not not_2 (not_2_out, Func[1]);
  not not_3 (not_3_out, A1);
  not not_4 (not_4_out, Func[2]);
  not not_5 (not_5_out, Func[0]);
  not not_6 (not_6_out, Func[1]);
  not not_7 (not_7_out, Func[0]);
  not not_8 (not_8_out, Op[5]);
  not not_9 (not_9_out, Func[3]);
  and and_1 (and_1_out, A1, not_1_out);
  and and_2 (and_2_out, A1, Func[2], not_2_out);
  and and_3 (and_3_out, not_3_out, A0);
  and and_4 (and_4_out, A0, not_4_out, Func[1], not_5_out);
  and and_5 (and_5_out, A0, Func[2], not_6_out, not_7_out);
  not not_10 (not_10_out, Op[4]);
  or or_1 (ALUOp[1], and_1_out, and_2_out);
  or or_2 (ALUOp[0], and_3_out, and_4_out, and_5_out);
  not not_11 (not_11_out, Op[3]);
  not not_12 (not_12_out, Op[1]);
  not not_13 (not_13_out, Op[2]);
  not not_14 (not_14_out, Op[0]);
  and R (R_out, not_14_out, not_12_out, not_13_out, not_9_out, not_11_out, not_10_out, not_8_out);
  and ori (ori_out, Op[0], not_12_out, Op[2], Op[3], not_10_out, not_8_out);
  and lw (lw_out, Op[0], Op[1], not_13_out, not_11_out, not_10_out, Op[5]);
  and sw (sw_out, Op[0], Op[1], not_13_out, Op[3], not_10_out, Op[5]);
  and beq (beq_out, not_14_out, not_12_out, Op[2], not_11_out, not_10_out, not_8_out);
  and lui (lui_out, Op[0], Op[1], Op[2], Op[3], not_10_out, not_8_out);
  and jal (jal_out, Op[0], Op[1], not_13_out, not_11_out, not_10_out, not_8_out);
  and jr (jr_out, not_14_out, not_12_out, not_13_out, Func[3], not_11_out, not_10_out, not_8_out);
  or u_RegWrite (RegWrite, R_out, lui_out, ori_out, jal_out, lw_out);
  or u_ALUSrc (ALUSrc, ori_out, lw_out, sw_out, lui_out);
  or NPCOp1 (NPCOp[1], jal_out, jr_out);
  or NPCOp0 (NPCOp[0], beq_out, jr_out);
  buf u_MemWrite (MemWrite, sw_out);  // OR_Gate
  or ALUOp1 (A1, R_out, ori_out);
  or ALUOp0 (A0, beq_out, R_out);
  buf EXTOp1 (EXTOp[1], lui_out);  // OR_Gate
  or EXTOp0 (EXTOp[0], lw_out, sw_out);
  buf RegDst0 (RegDst[0], R_out);  // OR_Gate
  buf RegDst1 (RegDst[1], jal_out);  // OR_Gate
  buf WDSrc1 (WDSrc[1], jal_out);  // OR_Gate
  buf WDSrc0 (WDSrc[0], lw_out);  // OR_Gate

  // Other names for the same wires on the sheet: f0 = Func[0]; f1 = Func[1]; f2 = Func[2]; f3 = Func[3]; f4 = Func[4];
  //   f5 = Func[5]
endmodule

module NPC (
  input  [1:0] NPCOp,
  input  [31:0] PC,
  input  [25:0] Imm,
  input  Zero,
  input  [31:0] RA,
  output [31:0] PC4,
  output [31:0] NPC
);

  wire [31:0] adder_2_out, bit_extender_1_out, multiplexer_1_out;

  Adder #(.width(32)) adder_1 (.a(PC), .b(32'h4), .out(PC4));  // open: cin, cout
  assign bit_extender_1_out = {{14{Imm[15]}}, {Imm[15:0], 2'b00}};  // Bit_Extender bit_extender_1
  Adder #(.width(32)) adder_2 (.a(PC4), .b(multiplexer_1_out), .out(adder_2_out));  // open: cin, cout
  Multiplexer #(.width(32)) multiplexer_1 (
    .in0({32{1'b0}}), .in1(bit_extender_1_out), .out(multiplexer_1_out), .sel(Zero));  // open: en
  Multiplexer #(.select(2), .width(32)) multiplexer_2 (
    .in0(PC4), .in1(adder_2_out), .in2({PC[31:28], Imm, 2'b00}), .in3(RA), .out(NPC), .sel(NPCOp));  // open: en

  // Other names for the same wires on the sheet: PCHigh[3:0] = PC[31:28]
endmodule
