// Logisim project 4bit_sort.circ as structural Verilog
module swap_sort (
  input  [3:0] in_1,
  input  [3:0] in_2,
  output [3:0] out_3,
  output [3:0] out_4
);

  wire comparator_1_gt;

  Comparator #(.width(4), .mode("unsigned")) comparator_1 (.a(in_1), .b(in_2), .gt(comparator_1_gt));  // open: eq, lt
  _4bit_swap u_4bit_swap_1 (.in_1(in_1), .in_2(in_2), .in_3(comparator_1_gt), .out_4(out_3), .out_5(out_4));
endmodule

module _1bit_swap (
  input  a,
  input  b,
  input  s,
  output c,
  output d
);

  wire and_1_out, and_2_out, and_3_out, and_4_out, not_1_out, not_2_out;

  not not_1 (not_1_out, s);
  not not_2 (not_2_out, s);
  and and_1 (and_1_out, b, s);
  and and_2 (and_2_out, a, not_1_out);
  and and_3 (and_3_out, b, not_2_out);
  and and_4 (and_4_out, a, s);
  or or_1 (c, and_1_out, and_2_out);
  or or_2 (d, and_3_out, and_4_out);
endmodule

module _4bit_swap (
  input  [3:0] in_1,
  input  [3:0] in_2,
  input  in_3,
  output [3:0] out_4,
  output [3:0] out_5
);

  _1bit_swap u_1bit_swap_1 (.a(in_1[0]), .b(in_2[0]), .s(in_3), .c(out_4[0]), .d(out_5[0]));
  _1bit_swap u_1bit_swap_2 (.a(in_1[1]), .b(in_2[1]), .s(in_3), .c(out_4[1]), .d(out_5[1]));
  _1bit_swap u_1bit_swap_3 (.a(in_1[2]), .b(in_2[2]), .s(in_3), .c(out_4[2]), .d(out_5[2]));
  _1bit_swap u_1bit_swap_4 (.a(in_1[3]), .b(in_2[3]), .s(in_3), .c(out_4[3]), .d(out_5[3]));
endmodule

module _4bit_sort (
  input  [3:0] A,
  input  [3:0] B,
  input  [3:0] C,
  input  [3:0] D,
  output [3:0] _1,
  output [3:0] _2,
  output [3:0] _3,
  output [3:0] _4
);

  wire [3:0] swap_sort_1_out_3, swap_sort_1_out_4, swap_sort_2_out_3, swap_sort_2_out_4, swap_sort_3_out_3,
       swap_sort_4_out_3, swap_sort_4_out_4, swap_sort_5_out_3;

  swap_sort swap_sort_1 (.in_1(A), .in_2(B), .out_3(swap_sort_1_out_3), .out_4(swap_sort_1_out_4));
  swap_sort swap_sort_2 (.in_1(swap_sort_1_out_4), .in_2(C), .out_3(swap_sort_2_out_3), .out_4(swap_sort_2_out_4));
  swap_sort swap_sort_3 (.in_1(swap_sort_2_out_4), .in_2(D), .out_3(swap_sort_3_out_3), .out_4(_4));
  swap_sort swap_sort_4 (
    .in_1(swap_sort_1_out_3), .in_2(swap_sort_2_out_3), .out_3(swap_sort_4_out_3), .out_4(swap_sort_4_out_4));
  swap_sort swap_sort_5 (.in_1(swap_sort_4_out_4), .in_2(swap_sort_3_out_3), .out_3(swap_sort_5_out_3), .out_4(_3));
  swap_sort swap_sort_6 (.in_1(swap_sort_4_out_3), .in_2(swap_sort_5_out_3), .out_3(_1), .out_4(_2));
endmodule
