// Logisim project fibonacci.circ as structural Verilog: 3 circuits, main circuit main
module main (
  input  [2:0] N,
  output [3:0] Nth
);

  wire count_num_1_freeze;
  wire [3:0] fib_1_out_2;

  count_num count_num_1 (.in_1(N), .freeze(count_num_1_freeze));
  fib fib_1 (.freeze(count_num_1_freeze), .out_2(fib_1_out_2));
  Multiplexer #(.width(4)) multiplexer_1 (
    .in0(4'b0000), .in1(fib_1_out_2), .out(Nth), .sel(count_num_1_freeze));  // open: en
endmodule

module count_num (
  input  [2:0] in_1,
  output freeze
);

  wire clock_1_out;
  wire [3:0] bit_extender_1_out, counter_1_q;

  assign bit_extender_1_out = {{1{1'b0}}, in_1};  // Bit_Extender bit_extender_1
  Counter #(.width(4), .max('hf), .ongoal("stay")) counter_1 (
    .Q(counter_1_q), .clk(clock_1_out));  // open: load, D, count, carry, clr
  Clock clock_1 (.out(clock_1_out));
  Comparator #(.width(4), .mode("unsigned")) comparator_1 (
    .a(bit_extender_1_out), .b(counter_1_q), .lt(freeze));  // open: gt, eq
endmodule

module fib (
  input  freeze,
  output [3:0] out_2
);

  wire clock, counter_1_q, work;
  wire [3:0] adder_1_out, multiplexer_1_out, prev;

  Clock clock_1 (.out(clock));
  not not_1 (work, freeze);
  Counter #(.width(1), .max('h1), .ongoal("stay")) counter_1 (
    .Q(counter_1_q), .clk(clock));  // open: load, D, count, carry, clr
  Multiplexer #(.width(4)) multiplexer_1 (
    .in0(4'b0001), .in1(out_2), .out(multiplexer_1_out), .sel(counter_1_q));  // open: en
  Adder #(.width(4)) adder_1 (.a(out_2), .b(prev), .out(adder_1_out));  // open: cin, cout
  Register #(.width(4)) register_1 (.D(multiplexer_1_out), .en(work), .Q(prev), .clk(clock));  // open: clr
  Register #(.width(4)) register_2 (.D(adder_1_out), .en(work), .Q(out_2), .clk(clock));  // open: clr

  // Other names for the same wires on the sheet: now[3:0] = out_2
endmodule
