// Logisim project mod5.circ as structural Verilog: 3 circuits, main circuit mod5
module mod5 (
  input  In,
  output out_2,
  output out_3,
  output out_4,
  output out_5,
  output out_6
);

  wire clock_1_out;
  wire [1:0] mealy1_1_out_3, register_1_q;

  Mealy1 mealy1_1 (.In(In), .in_2(register_1_q), .out_3(mealy1_1_out_3));
  Clock clock_1 (.out(clock_1_out));
  Register #(.width(2)) register_1 (.D(mealy1_1_out_3), .Q(register_1_q), .clk(clock_1_out));  // open: en, clr
  Mealy2 mealy2_1 (.In(In), .in_2(register_1_q), .s0(out_2), .s1(out_3), .s2(out_4), .s3(out_5), .s4(out_6));
endmodule

module Mealy1 (
  input  In,
  input  [1:0] in_2,
  output [1:0] out_3
);

  wire and_1_out, and_2_out, and_3_out, and_4_out, and_5_out, and_6_out, not_1_out, not_2_out, not_3_out,
       not_4_out, not_5_out, not_6_out, not_7_out, not_8_out;

  not not_1 (not_1_out, in_2[1]);
  not not_2 (not_2_out, in_2[0]);
  not not_3 (not_3_out, In);
  not not_4 (not_4_out, in_2[1]);
  not not_5 (not_5_out, In);
  not not_6 (not_6_out, in_2[0]);
  not not_7 (not_7_out, in_2[1]);
  not not_8 (not_8_out, in_2[0]);
  and and_1 (and_1_out, not_1_out, in_2[0]);
  and and_2 (and_2_out, in_2[1], not_2_out);
  and and_3 (and_3_out, not_3_out, not_4_out, in_2[0]);
  and and_4 (and_4_out, not_5_out, in_2[1], not_6_out);
  and and_5 (and_5_out, In, not_7_out, not_8_out);
  and and_6 (and_6_out, In, in_2[1], in_2[0]);
  or or_1 (out_3[1], and_1_out, and_2_out);
  or or_2 (out_3[0], and_3_out, and_4_out, and_5_out, and_6_out);
endmodule

module Mealy2 (
  input  In,
  input  [1:0] in_2,
  output s0,
  output s1,
  output s2,
  output s3,
  output s4
);

  wire and_1_out, and_2_out, and_3_out, and_4_out, and_5_out, and_6_out, and_7_out, and_8_out, not_1_out,
       not_2_out, not_3_out, not_4_out, not_5_out, not_6_out, not_7_out, not_8_out, not_9_out, not_10_out,
       not_11_out, not_12_out;

  not not_1 (not_1_out, In);
  not not_2 (not_2_out, in_2[0]);
  not not_3 (not_3_out, in_2[1]);
  not not_4 (not_4_out, In);
  not not_5 (not_5_out, in_2[0]);
  not not_6 (not_6_out, in_2[1]);
  not not_7 (not_7_out, in_2[0]);
  not not_8 (not_8_out, in_2[1]);
  not not_9 (not_9_out, In);
  not not_10 (not_10_out, in_2[0]);
  not not_11 (not_11_out, In);
  not not_12 (not_12_out, in_2[1]);
  and and_1 (and_1_out, not_1_out, not_2_out, not_3_out);
  and and_2 (and_2_out, not_4_out, in_2[0], in_2[1]);
  and and_3 (and_3_out, In, not_5_out, not_6_out);
  and and_4 (and_4_out, In, in_2[0], in_2[1]);
  and and_5 (and_5_out, In, not_7_out, in_2[1]);
  and and_6 (and_6_out, In, in_2[0], not_8_out);
  and and_7 (and_7_out, not_9_out, not_10_out, in_2[1]);
  and and_8 (and_8_out, not_11_out, in_2[0], not_12_out);
  or or_1 (s1, and_1_out, and_2_out);
  or or_2 (s2, and_3_out, and_4_out);
  or or_3 (s3, and_5_out, and_6_out);
  or or_4 (s4, and_7_out, and_8_out);

  assign s0 = 1'b0;
endmodule
